// Logisim project Atividade_LogiSim_01.circ as structural Verilog: 1 circuit, main circuit main
module main (
  input  A,
  input  A_2,
  input  B,
  input  B_2,
  input  C,
  input  C_2,
  input  A_3,
  input  W,
  input  B_3,
  input  Y,
  input  X,
  input  C_3,
  input  D,
  input  A_4,
  input  A_5,
  input  B_4,
  input  B_5,
  output out_18,
  output out_19,
  output out_20,
  output out_21,
  output out_22,
  output out_23
);

  wire A___B_out, A_B_out, A_C_out, and_1_out, and_2_out, and_3_out, n_B_C_out, n_C_D_out, nA_B_C_out,
       nB___C_out, nC_out, not_1_out, not_2_out, not_3_out, not_4_out, not_5_out, not_6_out, nY___W_out;

  not not_1 (not_1_out, B);
  or A___B (A___B_out, A_2, B);
  or nB___C (nB___C_out, not_1_out, C);
  and A_B (A_B_out, A_3, A_3, B_3);
  not nC (nC_out, C_3);
  and n_C_D (n_C_D_out, C_3, D);
  not not_2 (not_2_out, n_C_D_out);
  not not_3 (not_3_out, A_4);
  not not_4 (not_4_out, B_5);
  and A_C___n_B_C____nA_B_C (out_18, A___B_out, A___B_out, nB___C_out, nB___C_out);
  or A_B___nC___n_C_D (out_20, A_B_out, A_B_out, nC_out, not_2_out);
  and and_1 (and_1_out, not_3_out, B_5);
  and and_2 (and_2_out, A_4, not_4_out);
  or or_1 (out_22, and_1_out, and_2_out);
  not not_5 (not_5_out, A);
  not not_6 (not_6_out, Y);
  and A_C (A_C_out, A, C_2);
  and and_3 (and_3_out, B_2, C_2);
  and nA_B_C (nA_B_C_out, not_5_out, B_2, C_2);
  xor xor_1 (out_23, A_5, B_4);
  not n_B_C (n_B_C_out, and_3_out);
  or nY___W (nY___W_out, W, not_6_out);
  or or_2 (out_19, A_C_out, n_B_C_out, nA_B_C_out);
  and X__nY___W (out_21, nY___W_out, X);

  // Notes on the sheet:
  //   1.
  //   3.
  //   5.
  //   2.
  //   4.
endmodule
